# Fritzing sketch 5-button (saved by Fritzing 0.9.2b)
breadboards: 1

parts:
  S1 = Pushbutton [package="[THT]"]
  U1 = NodeMCU V1.0

nets:
  N1: S1.Pin_1, S1.Pin_2, U1.D2
  N2: S1.Pin_3, S1.Pin_4, U1.GND

custom parts:
  NodeMCU V1.0: ESP9266 based NodeMCU
