# Fritzing sketch nodemcu-deepsleep-dh11 (saved by Fritzing 0.9.2b)
breadboards: 1

parts:
  U1 = NodeMCU V1.0
  RHT1 = Humidity and Temperature Sensor RHT03

nets:
  N1: U1.D0, U1.RST
  N2: U1.D3, RHT1.Data-signal
  N3: U1.GND, RHT1.GND_2
  VIN: U1.Vin, RHT1.Vcc

custom parts:
  NodeMCU V1.0: ESP9266 based NodeMCU
