# Fritzing sketch pir-step-up (saved by Fritzing 0.9.2b)
breadboards: 1

parts:
  IC1 = Switching step-up voltage regulator [package=sot23-5]
  U1 = NodeMCU V1.0
  PIR2 = PIR sensor

nets:
  N1: IC1.EN, PIR2.VDD
  GND: IC1.OUT, U1.GND, PIR2.GND
  N2: IC1.NC, U1.3V3
  N3: U1.D3, PIR2.SIG

custom parts:
  NodeMCU V1.0: ESP9266 based NodeMCU
